# Fritzing sketch board1 (saved by Fritzing 0.9.3b)
stripboards: 5

parts:
  J1 = female pin header, 10 pins [form="♀ (female)"]
  J2 = female pin header, 10 pins [form="♀ (female)"]
  J3 = female pin header, 10 pins [form="♀ (female)"]
  J4 = female pin header, 10 pins [form="♀ (female)"]
  J5 = female pin header, 10 pins [form="♀ (female)"]
  J6 = female pin header, 10 pins [form="♀ (female)"]
  J7 = female pin header, 10 pins [form="♀ (female)"]
  J8 = female pin header, 10 pins [form="♀ (female)"]
  J9 = Screw terminal - 2 pins [package=THT]
  J10 = Screw terminal - 2 pins [package=THT]
  Part1 = Arduino Uno (Rev3)

nets:
  N1: J1.pin1, J2.pin1, J2.pin10, J3.pin1, J3.pin8, J4.pin1, J4.pin9, J5.pin1, J5.pin8, J5.pin9, J6.pin1, J6.pin3, J6.pin10, J7.pin1, J7.pin2, J7.pin10, J8.pin1, J8.pin2, J8.pin3, J8.pin10, J10.pin2, Part1.5V
  N2: J1.pin2, J2.pin9, J3.pin2, J4.pin2, J5.pin2, J6.pin9, J7.pin9, J8.pin9, J10.pin1, Part1.GND
  N3: J1.pin3, J2.pin8, J3.pin3, J4.pin3, J5.pin3, J6.pin8, J7.pin8, J8.pin8, J9.pin2, Part1.A5/SCL
  N4: J1.pin4, J2.pin7, J3.pin4, J4.pin4, J5.pin4, J6.pin7, J7.pin7, J8.pin7, J9.pin1, Part1.A4/SDA

notes:
  0
  1
  VCC
  GND
  SCL
  SDA
  A0
  A1
  A2
  RESET
  2
  3
  7
  5
  6
  4
