# Fritzing sketch level_shifter (saved by Fritzing 0.9.3b)
breadboards: 1

parts:
  Real_CD4504B = CD4048B [package="DIP (Dual Inline) [THT]"]
  Power_plug1 = Power plug [part_number=12V]
  Power_plug2 = Power plug [part_number=5V]
  Part1 = Arduino Uno (Rev3)
  BUTTONS_A_B_C = Toggle Switch [package=THT]
  BUTTONS_F_E_D = Toggle Switch [package=THT]

nets:
  N1: Real_CD4504B.J, Power_plug1.VCC, BUTTONS_A_B_C.L1
  N2: Real_CD4504B.Kd, Part1.A0
  N3: Real_CD4504B.H, Real_CD4504B.F, Real_CD4504B.Kb, BUTTONS_A_B_C.COM
  N4: Real_CD4504B.G, Part1.A1
  N5: Real_CD4504B.E, Part1.A2
  GND: Real_CD4504B.VSS, Real_CD4504B.B, Power_plug1.GND, Power_plug2.GND, BUTTONS_A_B_C.L2
  N6: Real_CD4504B.Kc, Real_CD4504B.D, Real_CD4504B.A, BUTTONS_F_E_D.COM
  N7: Real_CD4504B.Ka, Part1.A5/SCL
  N8: Real_CD4504B.C, Part1.A4/SDA
  N9: Real_CD4504B.EXPAND, Part1.A3
  VDD: Real_CD4504B.VDD, Power_plug2.VCC
